// Logisim project SIMD.circ as structural Verilog: 8 circuits, main circuit CPU
module CPU (
  input  [31:0] IP,
  input  [4:0] IP_Address,
  input  Manual_IR_CLK,
  input  Manual_IR,
  input  IP_2,
  input  CLK_IP,
  input  [31:0] IR,
  input  [31:0] Memory_Input_Address,
  input  Reset
);

  wire Clock_out, control_unit_1_hlt, control_unit_1_ir_en, control_unit_1_ir_ry_demux, control_unit_1_mux_b,
       control_unit_1_pc_inc, control_unit_1_pc_rz_mux, control_unit_1_ra_en, control_unit_1_rb_en,
       control_unit_1_read, control_unit_1_rf_write, control_unit_1_rm_en, control_unit_1_ry_en,
       control_unit_1_rz_en, control_unit_1_write, or_1_out, or_2_out, or_3_out, or_4_out, or_5_out;
  wire [1:0] control_unit_1_mux_y;
  wire [2:0] control_unit_1_alu_cu;
  wire [4:0] bit_splitter_1_address_ra, bit_splitter_1_address_rb, bit_splitter_1_address_rc,
       multiplexer_2_out;
  wire [5:0] bit_splitter_1_opcode;
  wire [31:0] alu_1_rz, bit_splitter_1_imm, memory_1_ir, memory_1_ry, multiplexer_1_out, multiplexer_3_out,
       multiplexer_4_out, multiplexer_5_out, multiplexer_6_out, program_counter_1_pc, RA_q, RB_q,
       register_1_q, register_file_1_ra, register_file_1_rb, RM_q, RY_q, RZ_q, undriven;

  Clock Clock (.out(Clock_out));
  or or_1 (or_1_out, Reset, control_unit_1_hlt);
  Multiplexer #(.width(32), .enable("false")) multiplexer_1 (.in0(RY_q), .in1(IP), .out(multiplexer_1_out), .sel(IP_2));
  or or_2 (or_2_out, IP_2, control_unit_1_rf_write);
  or or_3 (or_3_out, CLK_IP, Clock_out);
  Register #(.width(32)) RA (
    .D(register_file_1_ra), .en(control_unit_1_ra_en), .Q(RA_q), .clk(Clock_out), .clr(or_1_out));
  ALU alu_1 (.ALU_Control_Unit(control_unit_1_alu_cu), .RA(RA_q), .RB(multiplexer_3_out), .RZ(alu_1_rz));
  Multiplexer #(.width(5), .enable("false")) multiplexer_2 (
    .in0(bit_splitter_1_address_rc), .in1(IP_Address), .out(multiplexer_2_out), .sel(IP_2));
  Register #(.width(32)) RB (
    .D(register_file_1_rb), .en(control_unit_1_rb_en), .Q(RB_q), .clk(Clock_out), .clr(or_1_out));
  Multiplexer #(.width(32), .enable("false")) multiplexer_3 (
    .in0(RB_q), .in1(bit_splitter_1_imm), .out(multiplexer_3_out), .sel(control_unit_1_mux_b));
  Register #(.width(32)) RZ (.D(alu_1_rz), .en(control_unit_1_rz_en), .Q(RZ_q), .clk(Clock_out), .clr(or_1_out));
  Register_File register_file_1 (
    .RF_Write(or_2_out), .Address_RA(bit_splitter_1_address_ra), .Address_RB(bit_splitter_1_address_rb),
    .CLK(or_3_out), .Reset(or_1_out), .Address_RC(multiplexer_2_out), .RC(multiplexer_1_out),
    .RA(register_file_1_ra), .RB(register_file_1_rb));
  Multiplexer #(.select(2), .width(32), .enable("false")) multiplexer_4 (
    .in0(RZ_q), .in1(memory_1_ry), .in2(undriven), .out(multiplexer_4_out), .sel(control_unit_1_mux_y));  // open: in3
  Register #(.width(32)) RY (
    .D(multiplexer_4_out), .en(control_unit_1_ry_en), .Q(RY_q), .clk(Clock_out), .clr(or_1_out));
  Register #(.width(32)) RM (.D(RB_q), .en(control_unit_1_rm_en), .Q(RM_q), .clk(Clock_out), .clr(or_1_out));
  Bit_Splitter bit_splitter_1 (
    .IR(register_1_q), .Imm(bit_splitter_1_imm), .Address_RB(bit_splitter_1_address_rb),
    .Address_RA(bit_splitter_1_address_ra), .Address_RC(bit_splitter_1_address_rc),
    .Opcode(bit_splitter_1_opcode));
  Register #(.width(32)) register_1 (
    .D(memory_1_ir), .en(control_unit_1_ir_en), .Q(register_1_q), .clk(Clock_out), .clr(or_1_out));
  Control_Unit control_unit_1 (
    .Opcode(bit_splitter_1_opcode), .CLK(Clock_out), .Reset(or_1_out), .MUX_B(control_unit_1_mux_b),
    .IR_En(control_unit_1_ir_en), .PC_RZ_MUX(control_unit_1_pc_rz_mux), .PC_INC(control_unit_1_pc_inc),
    .RA_En(control_unit_1_ra_en), .RB_En(control_unit_1_rb_en), .RZ_En(control_unit_1_rz_en),
    .Read(control_unit_1_read), .Write(control_unit_1_write), .MUX_Y(control_unit_1_mux_y),
    .ALU_CU(control_unit_1_alu_cu), .RM_En(control_unit_1_rm_en), .RY_En(control_unit_1_ry_en),
    .RF_Write(control_unit_1_rf_write), .IR_RY_DEMUX(control_unit_1_ir_ry_demux), .HLT(control_unit_1_hlt));
  Program_Counter program_counter_1 (
    .RESET(or_1_out), .PC_INC(control_unit_1_pc_inc), .PC(program_counter_1_pc), .CLK(Clock_out));
  Multiplexer #(.width(32), .enable("false")) multiplexer_5 (
    .in0(program_counter_1_pc), .in1(Memory_Input_Address), .out(multiplexer_5_out), .sel(Manual_IR));
  or or_4 (or_4_out, control_unit_1_write, Manual_IR);
  Multiplexer #(.width(32), .enable("false")) multiplexer_6 (
    .in0(RM_q), .in1(IR), .out(multiplexer_6_out), .sel(Manual_IR));
  or or_5 (or_5_out, Clock_out, Manual_IR_CLK);
  Memory memory_1 (
    .IR_RY_DEMUX(control_unit_1_ir_ry_demux), .Read(control_unit_1_read), .Write(or_4_out), .RZ(RZ_q),
    .PC(multiplexer_5_out), .PC_RZ_MUX(control_unit_1_pc_rz_mux), .RM(multiplexer_6_out), .Reset(or_1_out),
    .IR(memory_1_ir), .RY(memory_1_ry), .CLK(or_5_out));
endmodule

module Register_File (
  input  [31:0] RC,
  input  RF_Write,
  input  [4:0] Address_RA,
  input  [4:0] Address_RC,
  input  [4:0] Address_RB,
  input  CLK,
  input  Reset,
  output [31:0] RA,
  output [31:0] RB
);

  wire demultiplexer_1_out0, demultiplexer_1_out1, demultiplexer_1_out2, demultiplexer_1_out3,
       demultiplexer_1_out4, demultiplexer_1_out5, demultiplexer_1_out6, demultiplexer_1_out7,
       demultiplexer_1_out8, demultiplexer_1_out9, demultiplexer_1_out10, demultiplexer_1_out11,
       demultiplexer_1_out12, demultiplexer_1_out13, demultiplexer_1_out14, demultiplexer_1_out15,
       demultiplexer_1_out16, demultiplexer_1_out17, demultiplexer_1_out18, demultiplexer_1_out19,
       demultiplexer_1_out20, demultiplexer_1_out21, demultiplexer_1_out22, demultiplexer_1_out23,
       demultiplexer_1_out24, demultiplexer_1_out25, demultiplexer_1_out26, demultiplexer_1_out27,
       demultiplexer_1_out28, demultiplexer_1_out29, demultiplexer_1_out30, demultiplexer_1_out31;
  wire [31:0] R0_q, R1_q, R2_q, R3_q, R4_q, R5_q, R6_q, R7_q, R8_q, R9_q, R10_q, R11_q, R12_q, R13_q, R14_q,
       R15_q, R16_q, R17_q, R18_q, R19_q, R20_q, R21_q, R22_q, R23_q, R24_q, R25_q, R26_q, R27_q, R28_q,
       R29_q, R30_q, R31_q;

  Demultiplexer #(.select(5), .enable("false")) demultiplexer_1 (
    .out0(demultiplexer_1_out0), .out1(demultiplexer_1_out1), .out2(demultiplexer_1_out2),
    .out3(demultiplexer_1_out3), .out4(demultiplexer_1_out4), .out5(demultiplexer_1_out5),
    .out6(demultiplexer_1_out6), .out7(demultiplexer_1_out7), .out8(demultiplexer_1_out8),
    .out9(demultiplexer_1_out9), .out10(demultiplexer_1_out10), .out11(demultiplexer_1_out11),
    .out12(demultiplexer_1_out12), .out13(demultiplexer_1_out13), .out14(demultiplexer_1_out14),
    .out15(demultiplexer_1_out15), .out16(demultiplexer_1_out16), .out17(demultiplexer_1_out17),
    .out18(demultiplexer_1_out18), .out19(demultiplexer_1_out19), .out20(demultiplexer_1_out20),
    .out21(demultiplexer_1_out21), .out22(demultiplexer_1_out22), .out23(demultiplexer_1_out23),
    .out24(demultiplexer_1_out24), .out25(demultiplexer_1_out25), .out26(demultiplexer_1_out26),
    .out27(demultiplexer_1_out27), .out28(demultiplexer_1_out28), .out29(demultiplexer_1_out29),
    .out30(demultiplexer_1_out30), .out31(demultiplexer_1_out31), .in(RF_Write), .sel(Address_RC));
  Register #(.width(32)) R0 (.D(RC), .en(demultiplexer_1_out0), .Q(R0_q), .clk(CLK), .clr(Reset));
  Register #(.width(32)) R4 (.D(RC), .en(demultiplexer_1_out4), .Q(R4_q), .clk(CLK), .clr(Reset));
  Register #(.width(32)) R8 (.D(RC), .en(demultiplexer_1_out8), .Q(R8_q), .clk(CLK), .clr(Reset));
  Register #(.width(32)) R12 (.D(RC), .en(demultiplexer_1_out12), .Q(R12_q), .clk(CLK), .clr(Reset));
  Register #(.width(32)) R16 (.D(RC), .en(demultiplexer_1_out16), .Q(R16_q), .clk(CLK), .clr(Reset));
  Register #(.width(32)) R20 (.D(RC), .en(demultiplexer_1_out20), .Q(R20_q), .clk(CLK), .clr(Reset));
  Register #(.width(32)) R24 (.D(RC), .en(demultiplexer_1_out24), .Q(R24_q), .clk(CLK), .clr(Reset));
  Register #(.width(32)) R28 (.D(RC), .en(demultiplexer_1_out28), .Q(R28_q), .clk(CLK), .clr(Reset));
  Register #(.width(32)) R1 (.D(RC), .en(demultiplexer_1_out1), .Q(R1_q), .clk(CLK), .clr(Reset));
  Register #(.width(32)) R5 (.D(RC), .en(demultiplexer_1_out5), .Q(R5_q), .clk(CLK), .clr(Reset));
  Register #(.width(32)) R9 (.D(RC), .en(demultiplexer_1_out9), .Q(R9_q), .clk(CLK), .clr(Reset));
  Register #(.width(32)) R13 (.D(RC), .en(demultiplexer_1_out13), .Q(R13_q), .clk(CLK), .clr(Reset));
  Register #(.width(32)) R17 (.D(RC), .en(demultiplexer_1_out17), .Q(R17_q), .clk(CLK), .clr(Reset));
  Register #(.width(32)) R21 (.D(RC), .en(demultiplexer_1_out21), .Q(R21_q), .clk(CLK), .clr(Reset));
  Register #(.width(32)) R25 (.D(RC), .en(demultiplexer_1_out25), .Q(R25_q), .clk(CLK), .clr(Reset));
  Register #(.width(32)) R29 (.D(RC), .en(demultiplexer_1_out29), .Q(R29_q), .clk(CLK), .clr(Reset));
  Register #(.width(32)) R2 (.D(RC), .en(demultiplexer_1_out2), .Q(R2_q), .clk(CLK), .clr(Reset));
  Register #(.width(32)) R6 (.D(RC), .en(demultiplexer_1_out6), .Q(R6_q), .clk(CLK), .clr(Reset));
  Register #(.width(32)) R10 (.D(RC), .en(demultiplexer_1_out10), .Q(R10_q), .clk(CLK), .clr(Reset));
  Register #(.width(32)) R14 (.D(RC), .en(demultiplexer_1_out14), .Q(R14_q), .clk(CLK), .clr(Reset));
  Register #(.width(32)) R18 (.D(RC), .en(demultiplexer_1_out18), .Q(R18_q), .clk(CLK), .clr(Reset));
  Register #(.width(32)) R22 (.D(RC), .en(demultiplexer_1_out22), .Q(R22_q), .clk(CLK), .clr(Reset));
  Register #(.width(32)) R26 (.D(RC), .en(demultiplexer_1_out26), .Q(R26_q), .clk(CLK), .clr(Reset));
  Register #(.width(32)) R30 (.D(RC), .en(demultiplexer_1_out30), .Q(R30_q), .clk(CLK), .clr(Reset));
  Register #(.width(32)) R3 (.D(RC), .en(demultiplexer_1_out3), .Q(R3_q), .clk(CLK), .clr(Reset));
  Register #(.width(32)) R7 (.D(RC), .en(demultiplexer_1_out7), .Q(R7_q), .clk(CLK), .clr(Reset));
  Register #(.width(32)) R11 (.D(RC), .en(demultiplexer_1_out11), .Q(R11_q), .clk(CLK), .clr(Reset));
  Register #(.width(32)) R15 (.D(RC), .en(demultiplexer_1_out15), .Q(R15_q), .clk(CLK), .clr(Reset));
  Register #(.width(32)) R19 (.D(RC), .en(demultiplexer_1_out19), .Q(R19_q), .clk(CLK), .clr(Reset));
  Register #(.width(32)) R23 (.D(RC), .en(demultiplexer_1_out23), .Q(R23_q), .clk(CLK), .clr(Reset));
  Register #(.width(32)) R27 (.D(RC), .en(demultiplexer_1_out27), .Q(R27_q), .clk(CLK), .clr(Reset));
  Register #(.width(32)) R31 (.D(RC), .en(demultiplexer_1_out31), .Q(R31_q), .clk(CLK), .clr(Reset));
  Multiplexer #(.select(5), .width(32)) multiplexer_1 (
    .in0(R0_q), .in1(R1_q), .in2(R2_q), .in3(R3_q), .in4(R4_q), .in5(R5_q), .in6(R6_q), .in7(R7_q),
    .in8(R8_q), .in9(R9_q), .in10(R10_q), .in11(R11_q), .in12(R12_q), .in13(R13_q), .in14(R14_q),
    .in15(R15_q), .in16(R16_q), .in17(R17_q), .in18(R18_q), .in19(R19_q), .in20(R20_q), .in21(R21_q),
    .in22(R22_q), .in23(R23_q), .in24(R24_q), .in25(R25_q), .in26(R26_q), .in27(R27_q), .in28(R28_q),
    .in29(R29_q), .in30(R30_q), .in31(R31_q), .out(RA), .sel(Address_RA), .en(1'b1));
  Multiplexer #(.select(5), .width(32)) multiplexer_2 (
    .in0(R0_q), .in1(R1_q), .in2(R2_q), .in3(R3_q), .in4(R4_q), .in5(R5_q), .in6(R6_q), .in7(R7_q),
    .in8(R8_q), .in9(R9_q), .in10(R10_q), .in11(R11_q), .in12(R12_q), .in13(R13_q), .in14(R14_q),
    .in15(R15_q), .in16(R16_q), .in17(R17_q), .in18(R18_q), .in19(R19_q), .in20(R20_q), .in21(R21_q),
    .in22(R22_q), .in23(R23_q), .in24(R24_q), .in25(R25_q), .in26(R26_q), .in27(R27_q), .in28(R28_q),
    .in29(R29_q), .in30(R30_q), .in31(R31_q), .out(RB), .sel(Address_RB), .en(1'b1));
endmodule

module ALU (
  input  [31:0] RA,
  input  [31:0] RB,
  input  [2:0] ALU_Control_Unit,
  output [31:0] RZ
);

  wire [31:0] adder_1_out, and_1_out, or_1_out, subtractor_1_out;

  Adder #(.width(32)) adder_1 (.a(RA), .b(RB), .out(adder_1_out));  // open: cin, cout
  Subtractor #(.width(32)) subtractor_1 (.a(RA), .b(RB), .out(subtractor_1_out));  // open: bin, bout
  assign and_1_out = RA & RB;  // AND_Gate and_1, 32 bits wide
  assign or_1_out = RA | RB;  // OR_Gate or_1, 32 bits wide
  Multiplexer #(.select(3), .width(32)) multiplexer_1 (
    .in0(adder_1_out), .in1(subtractor_1_out), .in2(and_1_out), .in3(or_1_out), .in4(RA), .in5(RB), .out(RZ),
    .sel(ALU_Control_Unit), .en(1'b1));  // open: in6, in7
endmodule

module Control_Unit (
  input  [5:0] Opcode,
  input  CLK,
  input  Reset,
  output HLT,
  output MUX_B,
  output IR_En,
  output PC_RZ_MUX,
  output PC_INC,
  output RA_En,
  output RB_En,
  output RZ_En,
  output Read,
  output IR_RY_DEMUX,
  output Write,
  output [1:0] MUX_Y,
  output [2:0] ALU_CU,
  output RM_En,
  output RY_En,
  output RF_Write
);

  wire and_1_out, and_5_out, decoder_1_out1, decoder_1_out3, decoder_1_out4, decoder_2_out0, decoder_2_out1,
       decoder_2_out2, decoder_2_out3, decoder_2_out4, decoder_2_out5, decoder_2_out6, decoder_2_out7,
       decoder_2_out8, decoder_2_out9, decoder_2_out10, decoder_2_out11, not_1_out, not_2_out, not_3_out,
       not_4_out, not_5_out, or_1_out, or_2_out, or_3_out, or_4_out, or_5_out, or_6_out, or_7_out, or_8_out,
       or_9_out;
  wire [2:0] counter_1_q;

  Counter #(.width(3), .max('h4)) counter_1 (.Q(counter_1_q), .clk(CLK), .clr(Reset));  // open: load, D, count, carry
  Decoder #(.select(3), .enable("false")) decoder_1 (
    .out0(IR_En), .out1(decoder_1_out1), .out2(RZ_En), .out3(decoder_1_out3), .out4(decoder_1_out4),
    .sel(counter_1_q));  // open: out5, out6, out7
  Decoder #(.select(5), .enable("false")) decoder_2 (
    .out0(decoder_2_out0), .out1(decoder_2_out1), .out2(decoder_2_out2), .out3(decoder_2_out3),
    .out4(decoder_2_out4), .out5(decoder_2_out5), .out6(decoder_2_out6), .out7(decoder_2_out7),
    .out8(decoder_2_out8), .out9(decoder_2_out9), .out10(decoder_2_out10), .out11(decoder_2_out11),
    .out12(HLT), .sel(Opcode[4:0]));  // open: out13, out14, out15, out16, out17, out18, out19, out20, out21, out22, out23, out24, out25, out26, out27, out28, out29, out30, out31
  or or_1 (or_1_out, decoder_2_out1, decoder_2_out2, decoder_2_out3, decoder_2_out5, decoder_2_out7, decoder_2_out9, decoder_2_out11);
  or or_2 (or_2_out, decoder_2_out4, decoder_2_out5, decoder_2_out6, decoder_2_out7, decoder_2_out8, decoder_2_out9, decoder_2_out10, decoder_2_out11);
  or or_3 (or_3_out, decoder_2_out6, decoder_2_out7);
  or or_4 (or_4_out, decoder_2_out8, decoder_2_out9);
  or or_5 (or_5_out, decoder_2_out10, decoder_2_out11);
  not not_1 (not_1_out, decoder_2_out0);
  and and_1 (and_1_out, or_2_out, decoder_1_out3);
  and and_2 (MUX_Y[0], decoder_2_out2, decoder_1_out3);
  and and_3 (MUX_Y[1], and_1_out, MUX_Y[0]);
  or or_6 (or_6_out, or_3_out, or_5_out, decoder_2_out1);
  or or_7 (or_7_out, or_4_out, or_5_out);
  or or_8 (or_8_out, decoder_2_out0, decoder_2_out1);
  and and_4 (MUX_B, or_1_out, RZ_En);
  not not_2 (not_2_out, or_1_out);
  or or_9 (or_9_out, not_2_out, decoder_2_out3);
  and and_5 (and_5_out, decoder_2_out2, decoder_1_out3);
  and and_6 (ALU_CU[0], or_6_out, RZ_En);
  and and_7 (ALU_CU[1], or_7_out, RZ_En);
  and and_8 (ALU_CU[2], RZ_En, or_8_out);
  not not_3 (not_3_out, HLT);
  not not_4 (not_4_out, decoder_2_out3);
  and and_9 (RA_En, decoder_1_out1, not_5_out);
  not not_5 (not_5_out, decoder_2_out1);
  and and_10 (RB_En, decoder_1_out1, not_1_out, or_9_out);
  or or_10 (Read, IR_En, and_5_out);
  and and_11 (IR_RY_DEMUX, decoder_2_out2, decoder_1_out3);
  and and_12 (Write, decoder_2_out3, decoder_1_out3);
  and and_13 (RM_En, decoder_2_out3, RZ_En);
  and and_14 (RY_En, not_3_out, not_4_out, decoder_1_out3);
  and and_15 (RF_Write, not_3_out, not_4_out, decoder_1_out4);

  assign PC_INC = IR_En;
  assign PC_RZ_MUX = IR_En;
endmodule

module Bit_Splitter (
  input  [31:0] IR,
  output [31:0] Imm,
  output [4:0] Address_RB,
  output [4:0] Address_RA,
  output [4:0] Address_RC,
  output [5:0] Opcode
);

  wire decoder_1_out0, decoder_1_out1, decoder_1_out2, decoder_1_out5, decoder_1_out7, decoder_1_out9,
       decoder_1_out11, or_1_out;
  wire [4:0] multiplexer_1_out;

  Decoder #(.select(4), .enable("false")) decoder_1 (
    .out0(decoder_1_out0), .out1(decoder_1_out1), .out2(decoder_1_out2), .out5(decoder_1_out5),
    .out7(decoder_1_out7), .out9(decoder_1_out9), .out11(decoder_1_out11), .sel(IR[29:26]));  // open: out3, out4, out6, out8, out10, out12, out13, out14, out15
  or or_1 (or_1_out, decoder_1_out0, decoder_1_out1, decoder_1_out2, decoder_1_out5, decoder_1_out7, decoder_1_out9, decoder_1_out11);
  Multiplexer #(.width(5), .enable("false")) multiplexer_1 (
    .in0({5{1'b0}}), .in1(IR[15:11]), .out(multiplexer_1_out), .sel(or_1_out));
  assign Imm = {{16{1'b0}}, {multiplexer_1_out, IR[10:0]}};  // Bit_Extender bit_extender_1

  assign Address_RA = IR[20:16];
  assign Address_RB = IR[15:11];
  assign Address_RC = IR[25:21];
  assign Opcode = IR[31:26];
endmodule

module Program_Counter (
  input  CLK,
  input  RESET,
  input  PC_INC,
  output [31:0] PC
);

  wire [31:0] adder_1_out, multiplexer_1_out;

  Register #(.width(32)) register_1 (.D(multiplexer_1_out), .Q(PC), .clk(CLK), .clr(RESET));  // open: en
  Multiplexer #(.width(32), .enable("false")) multiplexer_1 (
    .in0(PC), .in1(adder_1_out), .out(multiplexer_1_out), .sel(PC_INC));
  Adder #(.width(32)) adder_1 (.a(PC), .b(32'h1), .out(adder_1_out));  // open: cin, cout
endmodule

module Memory_File (
  input  [31:0] RM,
  input  Write,
  input  Read,
  input  [4:0] Read_Write_Address,
  input  CLK,
  input  Reset,
  output [31:0] RY
);

  wire demultiplexer_1_out0, demultiplexer_1_out1, demultiplexer_1_out2, demultiplexer_1_out3,
       demultiplexer_1_out4, demultiplexer_1_out5, demultiplexer_1_out6, demultiplexer_1_out7,
       demultiplexer_1_out8, demultiplexer_1_out9, demultiplexer_1_out10, demultiplexer_1_out11,
       demultiplexer_1_out12, demultiplexer_1_out13, demultiplexer_1_out14, demultiplexer_1_out15,
       demultiplexer_1_out16, demultiplexer_1_out17, demultiplexer_1_out18, demultiplexer_1_out19,
       demultiplexer_1_out20, demultiplexer_1_out21, demultiplexer_1_out22, demultiplexer_1_out23,
       demultiplexer_1_out24, demultiplexer_1_out25, demultiplexer_1_out26, demultiplexer_1_out27,
       demultiplexer_1_out28, demultiplexer_1_out29, demultiplexer_1_out30, demultiplexer_1_out31;
  wire [31:0] R0_q, R1_q, R2_q, R3_q, R4_q, R5_q, R6_q, R7_q, R8_q, R9_q, R10_q, R11_q, R12_q, R13_q, R14_q,
       R15_q, R16_q, R17_q, R18_q, R19_q, R20_q, R21_q, R22_q, R23_q, R24_q, R25_q, R26_q, R27_q, R28_q,
       R29_q, R30_q, R31_q;

  Demultiplexer #(.select(5), .enable("false")) demultiplexer_1 (
    .out0(demultiplexer_1_out0), .out1(demultiplexer_1_out1), .out2(demultiplexer_1_out2),
    .out3(demultiplexer_1_out3), .out4(demultiplexer_1_out4), .out5(demultiplexer_1_out5),
    .out6(demultiplexer_1_out6), .out7(demultiplexer_1_out7), .out8(demultiplexer_1_out8),
    .out9(demultiplexer_1_out9), .out10(demultiplexer_1_out10), .out11(demultiplexer_1_out11),
    .out12(demultiplexer_1_out12), .out13(demultiplexer_1_out13), .out14(demultiplexer_1_out14),
    .out15(demultiplexer_1_out15), .out16(demultiplexer_1_out16), .out17(demultiplexer_1_out17),
    .out18(demultiplexer_1_out18), .out19(demultiplexer_1_out19), .out20(demultiplexer_1_out20),
    .out21(demultiplexer_1_out21), .out22(demultiplexer_1_out22), .out23(demultiplexer_1_out23),
    .out24(demultiplexer_1_out24), .out25(demultiplexer_1_out25), .out26(demultiplexer_1_out26),
    .out27(demultiplexer_1_out27), .out28(demultiplexer_1_out28), .out29(demultiplexer_1_out29),
    .out30(demultiplexer_1_out30), .out31(demultiplexer_1_out31), .in(Write), .sel(Read_Write_Address));
  Register #(.width(32)) R0 (.D(RM), .en(demultiplexer_1_out0), .Q(R0_q), .clk(CLK), .clr(Reset));
  Register #(.width(32)) R4 (.D(RM), .en(demultiplexer_1_out4), .Q(R4_q), .clk(CLK), .clr(Reset));
  Register #(.width(32)) R8 (.D(RM), .en(demultiplexer_1_out8), .Q(R8_q), .clk(CLK), .clr(Reset));
  Register #(.width(32)) R12 (.D(RM), .en(demultiplexer_1_out12), .Q(R12_q), .clk(CLK), .clr(Reset));
  Register #(.width(32)) R16 (.D(RM), .en(demultiplexer_1_out16), .Q(R16_q), .clk(CLK), .clr(Reset));
  Register #(.width(32)) R20 (.D(RM), .en(demultiplexer_1_out20), .Q(R20_q), .clk(CLK), .clr(Reset));
  Register #(.width(32)) R24 (.D(RM), .en(demultiplexer_1_out24), .Q(R24_q), .clk(CLK), .clr(Reset));
  Register #(.width(32)) R28 (.D(RM), .en(demultiplexer_1_out28), .Q(R28_q), .clk(CLK), .clr(Reset));
  Register #(.width(32)) R1 (.D(RM), .en(demultiplexer_1_out1), .Q(R1_q), .clk(CLK), .clr(Reset));
  Register #(.width(32)) R5 (.D(RM), .en(demultiplexer_1_out5), .Q(R5_q), .clk(CLK), .clr(Reset));
  Register #(.width(32)) R9 (.D(RM), .en(demultiplexer_1_out9), .Q(R9_q), .clk(CLK), .clr(Reset));
  Register #(.width(32)) R13 (.D(RM), .en(demultiplexer_1_out13), .Q(R13_q), .clk(CLK), .clr(Reset));
  Register #(.width(32)) R17 (.D(RM), .en(demultiplexer_1_out17), .Q(R17_q), .clk(CLK), .clr(Reset));
  Register #(.width(32)) R21 (.D(RM), .en(demultiplexer_1_out21), .Q(R21_q), .clk(CLK), .clr(Reset));
  Register #(.width(32)) R25 (.D(RM), .en(demultiplexer_1_out25), .Q(R25_q), .clk(CLK), .clr(Reset));
  Register #(.width(32)) R29 (.D(RM), .en(demultiplexer_1_out29), .Q(R29_q), .clk(CLK), .clr(Reset));
  Register #(.width(32)) R2 (.D(RM), .en(demultiplexer_1_out2), .Q(R2_q), .clk(CLK), .clr(Reset));
  Register #(.width(32)) R6 (.D(RM), .en(demultiplexer_1_out6), .Q(R6_q), .clk(CLK), .clr(Reset));
  Register #(.width(32)) R10 (.D(RM), .en(demultiplexer_1_out10), .Q(R10_q), .clk(CLK), .clr(Reset));
  Register #(.width(32)) R14 (.D(RM), .en(demultiplexer_1_out14), .Q(R14_q), .clk(CLK), .clr(Reset));
  Register #(.width(32)) R18 (.D(RM), .en(demultiplexer_1_out18), .Q(R18_q), .clk(CLK), .clr(Reset));
  Register #(.width(32)) R22 (.D(RM), .en(demultiplexer_1_out22), .Q(R22_q), .clk(CLK), .clr(Reset));
  Register #(.width(32)) R26 (.D(RM), .en(demultiplexer_1_out26), .Q(R26_q), .clk(CLK), .clr(Reset));
  Register #(.width(32)) R30 (.D(RM), .en(demultiplexer_1_out30), .Q(R30_q), .clk(CLK), .clr(Reset));
  Register #(.width(32)) R3 (.D(RM), .en(demultiplexer_1_out3), .Q(R3_q), .clk(CLK), .clr(Reset));
  Register #(.width(32)) R7 (.D(RM), .en(demultiplexer_1_out7), .Q(R7_q), .clk(CLK), .clr(Reset));
  Register #(.width(32)) R11 (.D(RM), .en(demultiplexer_1_out11), .Q(R11_q), .clk(CLK), .clr(Reset));
  Register #(.width(32)) R15 (.D(RM), .en(demultiplexer_1_out15), .Q(R15_q), .clk(CLK), .clr(Reset));
  Register #(.width(32)) R19 (.D(RM), .en(demultiplexer_1_out19), .Q(R19_q), .clk(CLK), .clr(Reset));
  Register #(.width(32)) R23 (.D(RM), .en(demultiplexer_1_out23), .Q(R23_q), .clk(CLK), .clr(Reset));
  Register #(.width(32)) R27 (.D(RM), .en(demultiplexer_1_out27), .Q(R27_q), .clk(CLK), .clr(Reset));
  Register #(.width(32)) R31 (.D(RM), .en(demultiplexer_1_out31), .Q(R31_q), .clk(CLK), .clr(Reset));
  Multiplexer #(.select(5), .width(32)) multiplexer_1 (
    .in0(R0_q), .in1(R1_q), .in2(R2_q), .in3(R3_q), .in4(R4_q), .in5(R5_q), .in6(R6_q), .in7(R7_q),
    .in8(R8_q), .in9(R9_q), .in10(R10_q), .in11(R11_q), .in12(R12_q), .in13(R13_q), .in14(R14_q),
    .in15(R15_q), .in16(R16_q), .in17(R17_q), .in18(R18_q), .in19(R19_q), .in20(R20_q), .in21(R21_q),
    .in22(R22_q), .in23(R23_q), .in24(R24_q), .in25(R25_q), .in26(R26_q), .in27(R27_q), .in28(R28_q),
    .in29(R29_q), .in30(R30_q), .in31(R31_q), .out(RY), .sel(Read_Write_Address), .en(Read));
endmodule

module Memory (
  input  IR_RY_DEMUX,
  input  Read,
  input  Write,
  input  [31:0] RZ,
  input  [31:0] PC,
  input  PC_RZ_MUX,
  input  [31:0] RM,
  input  CLK,
  input  Reset,
  output [31:0] IR,
  output [31:0] RY
);

  wire [31:0] memory_file_1_ry, multiplexer_1_out;

  Demultiplexer #(.width(32), .enable("false")) demultiplexer_1 (
    .out0(IR), .out1(RY), .in(memory_file_1_ry), .sel(IR_RY_DEMUX));
  Multiplexer #(.width(32), .enable("false")) multiplexer_1 (
    .in0(RZ), .in1(PC), .out(multiplexer_1_out), .sel(PC_RZ_MUX));
  Memory_File memory_file_1 (
    .Write(Write), .Read_Write_Address(multiplexer_1_out[4:0]), .CLK(CLK), .Reset(Reset), .Read(Read),
    .RM(RM), .RY(memory_file_1_ry));
endmodule
